// Logisim project 7SIG.circ as structural Verilog: 1 circuit, main circuit main
module main (
);

  wire A_p1, A_p2, B_p2, D_p2, n7447_1_pin8, n7447_1_pin9, n7447_1_pin10, n7447_1_pin11, n7447_1_pin12,
       n7447_1_pin13, n7447_1_pin14, n7447_1_pin15, switch_3_p2;

  // Switch A: pin names not known; wires that end beside it: A_p1, A_p2
  // Switch switch_1: pin names not known
  // Switch B: pin names not known; wires that end beside it: A_p1, B_p2
  // Switch switch_2: pin names not known
  // Switch switch_3: pin names not known; wires that end beside it: A_p1, switch_3_p2
  // Switch C: pin names not known
  // Switch D: pin names not known; wires that end beside it: A_p1, D_p2
  // Switch switch_4: pin names not known
  Pull_Resistor pull_resistor_1 (.node(B_p2));
  Pull_Resistor pull_resistor_2 (.node(A_p2));
  Pull_Resistor pull_resistor_3 (.node(D_p2));
  Pull_Resistor pull_resistor_4 (.node(switch_3_p2));
  _7447 #(.ShowInternalStructure("true"), .VccGndPorts("true")) u_7447_1 (
    .pin1(B_p2), .pin2(switch_3_p2), .pin3(A_p1), .pin4(A_p1), .pin5(A_p1), .pin6(D_p2), .pin7(A_p2),
    .pin8(n7447_1_pin8), .pin16(A_p1), .pin15(n7447_1_pin15), .pin14(n7447_1_pin14), .pin13(n7447_1_pin13),
    .pin12(n7447_1_pin12), .pin11(n7447_1_pin11), .pin10(n7447_1_pin10), .pin9(n7447_1_pin9));
  _7447 #(.ShowInternalStructure("true"), .VccGndPorts("true")) u_7447_2 (
    .pin1(B_p2), .pin2(switch_3_p2), .pin3(A_p1), .pin4(A_p1), .pin5(A_p1), .pin6(D_p2), .pin7(A_p2),
    .pin8(n7447_1_pin8), .pin16(A_p1), .pin15(n7447_1_pin15), .pin14(n7447_1_pin14), .pin13(n7447_1_pin13),
    .pin12(n7447_1_pin12), .pin11(n7447_1_pin11), .pin10(n7447_1_pin10), .pin9(n7447_1_pin9));
  _7_Segment_Display #(.active("false")) u_7_segment_display_1 (
    .g(n7447_1_pin14), .f(n7447_1_pin15), .a(n7447_1_pin13), .b(n7447_1_pin12), .e(n7447_1_pin9),
    .d(n7447_1_pin10), .c(n7447_1_pin11), .dp(n7447_1_pin8));
  // also tied to GND on the sheet: n7447_1_pin8
  // also tied to VCC on the sheet: A_p1
endmodule
